// Logisim project I-ésimo Término de Collatz (Problema 9).circ as structural Verilog
module BOARD_BIG_ASM (
  output out_1
);

  wire button_1_out, CLK, CLR, d_ff_1_q, not_1_out, Write, Write_ASCII;
  wire [6:0] ASCII;
  wire [7:0] counter_1_q;
  wire [23:0] Dir_INPUT, Dir_MEMORY;
  wire [31:0] INPUT, MEMORY_IN, MEMORY_OUT;

  Button button_1 (.out(button_1_out));
  Clock clock_1 (.out(CLK));
  D_Flip_Flop d_ff_1 (.clk(CLK), .D(1'b1), .Q(d_ff_1_q), .reset(button_1_out));  // open: Qn, preset, en
  D_Flip_Flop d_ff_2 (.clk(CLK), .D(d_ff_1_q), .Qn(CLR), .reset(button_1_out));  // open: Q, preset, en
  BIG_ASM big_asm_1 (
    .DATA_INPUT(INPUT), .MEMORY_IN(MEMORY_OUT), .CLK(CLK), .CLR(CLR), .DIR_INPUT(Dir_INPUT),
    .MEMORY_OUT(MEMORY_IN), .DIR_MEMORY(Dir_MEMORY), .Write_OUTPUT(Write), .ASCII(ASCII),
    .Write_ASCII(Write_ASCII), .END(out_1));
  MEMORY memory_1 (.DIR(Dir_MEMORY), .DATA_IN(MEMORY_IN), .WRITE(Write), .CLK(CLK), .CLR(CLR), .DATA_OUT(MEMORY_OUT));
  INPUT input_1 (.DIR(Dir_INPUT), .CLK(CLK), .DATA_OUT(INPUT));
  Counter counter_1 (.load(1'b0), .count(not_1_out), .Q(counter_1_q), .clk(CLK), .clr(CLR));  // open: D, carry
  not not_1 (not_1_out, out_1);
  // Probe on counter_1_q
  TTY #(.rows(32), .cols(60)) tty_1 (.data(ASCII), .clk(CLK), .we(Write_ASCII), .clr(CLR));

  // Other names for the same wires on the sheet: END = out_1

  // Notes on the sheet:
  //   COUNTER
  //   BOARD
endmodule

module INPUT (
  input  [23:0] DIR,
  input  CLK,
  output [31:0] DATA_OUT
);

  RAM #(.addrWidth(24), .dataWidth(32)) ram_1 (.addr(DIR), .data(DATA_OUT), .clk(CLK), .ld(1'b1));  // open: sel, clr
endmodule

module MEMORY (
  input  [23:0] DIR,
  input  [31:0] DATA_IN,
  input  WRITE,
  input  CLK,
  input  CLR,
  output [31:0] DATA_OUT
);

  wire not_1_out;

  not not_1 (not_1_out, WRITE);
  RAM #(.addrWidth(24), .dataWidth(32), .bus("separate")) ram_1 (
    .addr(DIR), .din(DATA_IN), .data(DATA_OUT), .clk(CLK), .ld(not_1_out), .clr(CLR));  // open: str, sel
endmodule

module BIG_ASM (
  input  [31:0] DATA_INPUT,
  input  [31:0] MEMORY_IN,
  input  CLK,
  input  CLR,
  output [23:0] DIR_INPUT,
  output [31:0] MEMORY_OUT,
  output [23:0] DIR_MEMORY,
  output Write_OUTPUT,
  output [6:0] ASCII,
  output Write_ASCII,
  output END
);

  wire cu_1_l_i, cu_1_l_n, cu_1_l_t, cu_1_out_11, cu_1_s_t, d_ff_1_q, end0, n_2__0, or_1_out, t_i;
  wire [1:0] cu_1_out_10;
  wire [31:0] datapath_1_out_11;

  CU cu_1 (
    .CLR(CLR), .CLK(CLK), .in_3(n_2__0), .in_4(t_i), .L_n(cu_1_l_n), .L_i(cu_1_l_i), .S_t(cu_1_s_t),
    .L_t(cu_1_l_t), .out_10(cu_1_out_10), .out_11(cu_1_out_11), .out_5(end0));
  DataPath datapath_1 (
    .IOUT(DATA_INPUT), .CLR(CLR), .CLK(CLK), .L_n(cu_1_l_n), .L_i(cu_1_l_i), .S_t(cu_1_s_t), .L_t(cu_1_l_t),
    .in_8(cu_1_out_10), .in_9(cu_1_out_11), .DirInput(DIR_INPUT), .t_i(t_i), .out_13(n_2__0),
    .out_11(datapath_1_out_11));
  PRINT_DEC print_dec_1 (
    .num(datapath_1_out_11), .start(end0), .CLK(CLK), .RST(CLR), .ASCII(ASCII), .Write_ASCII(Write_ASCII),
    .END(END));
  or or_1 (or_1_out, END, d_ff_1_q);
  D_Flip_Flop d_ff_1 (.clk(CLK), .D(or_1_out), .Q(d_ff_1_q), .reset(CLR));  // open: Qn, preset, en

  // Other names for the same wires on the sheet: rst = CLR
endmodule

module PRINT_UDEC (
  input  [31:0] num,
  input  start,
  input  CLK,
  input  RST,
  output [6:0] ASCII,
  output Write_ASCII,
  output \end 
);

  wire _0_c, _0_n, demultiplexer_1_out0, demultiplexer_2_out0, demultiplexer_2_out1, demultiplexer_3_out0,
       demultiplexer_3_out1, IDLE_2_q, IDLE_3_q, IDLE_4_q, IDLE_q, Lc, Lc_0, Ln, Ln_0, or_1_out;
  wire [23:0] bit_extender_1_out;
  wire [31:0] c, c___1, c___1_t, divider_1_rem, memory_1_data_out, multiplexer_1_out, multiplexer_2_out,
       multiplexer_3_out, n, n___10, n___10___48;

  Multiplexer #(.width(32), .enable("false")) multiplexer_1 (
    .in0(num), .in1(n___10), .out(multiplexer_1_out), .sel(Lc_0));
  Divider #(.width(32)) divider_1 (.a(n), .b(32'ha), .out(n___10), .rem(divider_1_rem));  // open: upper
  Adder #(.width(32)) adder_1 (.a(divider_1_rem), .b(32'h30), .out(n___10___48));  // open: cin, cout
  or or_1 (or_1_out, demultiplexer_1_out0, \end );
  Register #(.width(32)) u_n (.D(multiplexer_1_out), .en(Ln), .Q(n), .clk(CLK), .clr(RST));
  D_Flip_Flop IDLE (.clk(CLK), .D(or_1_out), .Q(IDLE_q), .preset(RST));  // open: Qn, en, reset
  Demultiplexer #(.enable("false")) demultiplexer_1 (
    .out0(demultiplexer_1_out0), .out1(Ln_0), .in(IDLE_q), .sel(start));
  or or_2 (Write_ASCII, demultiplexer_3_out0, demultiplexer_2_out1);
  Multiplexer #(.width(32), .enable("false")) multiplexer_2 (
    .in0(c___1), .in1(c___1_t), .out(multiplexer_2_out), .sel(Write_ASCII));
  Adder #(.width(32)) adder_2 (.a(c), .b(32'h1), .out(c___1));  // open: cin, cout
  Subtractor #(.width(32)) subtractor_1 (.a(c), .b(32'h1), .out(c___1_t));  // open: bin, bout
  D_Flip_Flop IDLE_2 (.clk(CLK), .D(Ln_0), .Q(IDLE_2_q), .reset(RST));  // open: Qn, preset, en
  Register #(.width(32)) u_c (.D(multiplexer_2_out), .en(Lc), .Q(c), .clk(CLK), .clr(RST));
  or or_3 (Lc_0, IDLE_2_q, demultiplexer_3_out1);
  Multiplexer #(.width(32), .enable("false")) multiplexer_3 (
    .in0(c), .in1(c___1_t), .out(multiplexer_3_out), .sel(Write_ASCII));
  Comparator #(.width(32), .mode("unsigned")) comparator_1 (.a({32{1'b0}}), .b(n), .lt(_0_n));  // open: gt, eq
  Comparator #(.width(32), .mode("unsigned")) comparator_2 (.a({32{1'b0}}), .b(c), .lt(_0_c));  // open: gt, eq
  D_Flip_Flop IDLE_3 (.clk(CLK), .D(Write_ASCII), .Q(IDLE_3_q), .reset(RST));  // open: Qn, preset, en
  Demultiplexer #(.enable("false")) demultiplexer_2 (
    .out0(demultiplexer_2_out0), .out1(demultiplexer_2_out1), .in(IDLE_3_q), .sel(_0_c));
  Bit_Extender #(.in_width(32), .out_width(24)) bit_extender_1 (.in(multiplexer_3_out), .out(bit_extender_1_out));
  D_Flip_Flop IDLE_4 (.clk(CLK), .D(Lc_0), .Q(IDLE_4_q), .reset(RST));  // open: Qn, preset, en
  or or_4 (Lc, Lc_0, Write_ASCII);
  or or_5 (Ln, Ln_0, Lc_0);
  Demultiplexer #(.enable("false")) demultiplexer_3 (
    .out0(demultiplexer_3_out0), .out1(demultiplexer_3_out1), .in(IDLE_4_q), .sel(_0_n));
  D_Flip_Flop IDLE_5 (.clk(CLK), .D(demultiplexer_2_out0), .Q(\end ), .reset(RST));  // open: Qn, preset, en
  MEMORY memory_1 (
    .DIR(bit_extender_1_out), .DATA_IN(n___10___48), .WRITE(Lc_0), .CLK(CLK), .CLR(RST),
    .DATA_OUT(memory_1_data_out));
  Bit_Extender #(.in_width(32), .out_width(7)) bit_extender_2 (.in(memory_1_data_out), .out(ASCII));

  // Other names for the same wires on the sheet: Lc_1 = Write_ASCII; Sc = Write_ASCII; Ln_1 = Lc_0; Sn = Lc_0;
  //   Write = Lc_0
endmodule

module PRINT_DEC (
  input  [31:0] num,
  input  start,
  input  CLK,
  input  RST,
  output [6:0] ASCII,
  output Write_ASCII,
  output END
);

  wire demultiplexer_1_out0, demultiplexer_1_out1, demultiplexer_2_out0, demultiplexer_3_out0, end_t,
       IDLE_3_q, IDLE_q, or_1_out, or_2_out, or_3_out, S_ASCII, startUDEC, Write_ASCII_1;
  wire [6:0] ASCII_t;
  wire [31:0] multiplexer_1_out, negator_1_out;

  or or_1 (or_1_out, demultiplexer_1_out0, END);
  Negator #(.width(32)) negator_1 (.in(num), .out(negator_1_out));
  D_Flip_Flop IDLE (.clk(CLK), .D(or_1_out), .Q(IDLE_q), .preset(RST));  // open: Qn, en, reset
  Demultiplexer #(.enable("false")) demultiplexer_1 (
    .out0(demultiplexer_1_out0), .out1(demultiplexer_1_out1), .in(IDLE_q), .sel(start));
  Multiplexer #(.width(32), .enable("false")) multiplexer_1 (
    .in0(num), .in1(negator_1_out), .out(multiplexer_1_out), .sel(num[31]));
  Demultiplexer #(.enable("false")) demultiplexer_2 (
    .out0(demultiplexer_2_out0), .out1(S_ASCII), .in(demultiplexer_1_out1), .sel(num[31]));
  or or_2 (or_2_out, demultiplexer_2_out0, S_ASCII);
  D_Flip_Flop IDLE_2 (.clk(CLK), .D(or_2_out), .Q(startUDEC), .reset(RST));  // open: Qn, preset, en
  PRINT_UDEC print_udec_1 (
    .num(multiplexer_1_out), .start(startUDEC), .CLK(CLK), .RST(RST), .ASCII(ASCII_t),
    .Write_ASCII(Write_ASCII_1), .\end (end_t));
  D_Flip_Flop IDLE_3 (.clk(CLK), .D(or_3_out), .Q(IDLE_3_q), .reset(RST));  // open: Qn, preset, en
  or or_3 (or_3_out, startUDEC, demultiplexer_3_out0);
  Demultiplexer #(.enable("false")) demultiplexer_3 (
    .out0(demultiplexer_3_out0), .out1(END), .in(IDLE_3_q), .sel(end_t));
  Multiplexer #(.width(7), .enable("false")) multiplexer_2 (
    .in0(ASCII_t), .in1(7'b0101101), .out(ASCII), .sel(S_ASCII));
  or or_4 (Write_ASCII, S_ASCII, Write_ASCII_1);

  // Other names for the same wires on the sheet: sign = num[31]; Write_ASCII_0 = S_ASCII
endmodule

module TEST_PRINT (
  input  [31:0] in_1,
  output out_2
);

  wire button_1_out, button_2_out, CLK, CLR, d_ff_1_q, Write_ASCII;
  wire [6:0] ASCII;

  Button button_1 (.out(button_1_out));
  Clock clock_1 (.out(CLK));
  D_Flip_Flop d_ff_1 (.clk(CLK), .D(1'b1), .Q(d_ff_1_q), .reset(button_1_out));  // open: Qn, preset, en
  D_Flip_Flop d_ff_2 (.clk(CLK), .D(d_ff_1_q), .Qn(CLR), .reset(button_1_out));  // open: Q, preset, en
  Button button_2 (.out(button_2_out));
  PRINT_UDEC print_udec_1 ();  // open: num, start, CLK, RST, ASCII, Write_ASCII, end
  PRINT_DEC print_dec_1 (
    .num(in_1), .start(button_2_out), .CLK(CLK), .RST(CLR), .ASCII(ASCII), .Write_ASCII(Write_ASCII),
    .END(out_2));
  TTY #(.rows(32), .cols(60)) tty_1 (.data(ASCII), .clk(CLK), .we(Write_ASCII), .clr(CLR));
endmodule

module DataPath (
  input  [31:0] IOUT,
  input  CLR,
  input  CLK,
  input  L_n,
  input  L_i,
  input  S_t,
  input  L_t,
  input  [1:0] in_8,
  input  in_9,
  output [23:0] DirInput,
  output [31:0] out_11,
  output t_i,
  output out_13
);

  wire [31:0] _3n_1, i, multiplexer_1_out, multiplexer_2_out, multiplier_1_out, n_2, n_2_t, t, t_1;

  Multiplexer #(.width(32)) multiplexer_1 (
    .in0({32{1'b0}}), .in1(t_1), .out(multiplexer_1_out), .sel(S_t));  // open: en
  Register #(.width(32)) u_i (.D(IOUT), .en(L_i), .Q(i), .clk(CLK), .clr(CLR));
  Register #(.width(32)) u_t (.D(multiplexer_1_out), .en(L_t), .Q(t), .clk(CLK), .clr(CLR));
  Divider #(.width(32)) divider_1 (.a(out_11), .b(32'h2), .out(n_2_t), .rem(n_2));  // open: upper
  Comparator #(.width(32), .mode("unsigned")) comparator_1 (.a(n_2), .b({32{1'b0}}), .eq(out_13));  // open: gt, lt
  Adder #(.width(32)) adder_1 (.a(t), .b(32'h1), .out(t_1));  // open: cin, cout
  Multiplier #(.width(32)) multiplier_1 (.a(out_11), .b(32'h3), .out(multiplier_1_out));  // open: cin, cout
  Multiplexer #(.select(2), .width(32)) multiplexer_2 (
    .in0(IOUT), .in1(n_2_t), .in2(_3n_1), .out(multiplexer_2_out), .sel(in_8));  // open: in3, en
  Register #(.width(32)) n (.D(multiplexer_2_out), .en(L_n), .Q(out_11), .clk(CLK), .clr(CLR));
  Adder #(.width(32)) adder_2 (.a(multiplier_1_out), .b(32'h1), .out(_3n_1));  // open: cin, cout
  Comparator #(.width(32), .mode("unsigned")) comparator_2 (.a(t), .b(i), .lt(t_i));  // open: gt, eq
  Multiplexer #(.width(24)) multiplexer_3 (.in0({24{1'b0}}), .in1(24'h1), .out(DirInput), .sel(in_9));  // open: en

  // Other names for the same wires on the sheet: n[31:0] = out_11; n_2__0 = out_13; S_n[1:0] = in_8; SDir = in_9
endmodule

module CU (
  input  CLR,
  input  CLK,
  input  in_3,
  input  in_4,
  output out_5,
  output L_n,
  output L_i,
  output S_t,
  output L_t,
  output [1:0] out_10,
  output out_11
);

  wire demultiplexer_1_out0, demultiplexer_1_out1, demultiplexer_2_out1, GetC_q, IDLE_q, L_n0, not_1_out,
       or_1_out, or_2_out, while_q;

  D_Flip_Flop IDLE (.clk(CLK), .D(demultiplexer_1_out0), .Q(IDLE_q), .preset(CLR));  // open: Qn, en, reset
  Demultiplexer demultiplexer_1 (
    .out0(demultiplexer_1_out0), .out1(demultiplexer_1_out1), .in(IDLE_q), .sel(1'b1));  // open: en
  D_Flip_Flop \wait  (.clk(CLK), .D(demultiplexer_1_out1), .Q(L_n0), .reset(CLR));  // open: Qn, preset, en
  D_Flip_Flop GetA (.clk(CLK), .D(L_n0), .Q(L_i), .reset(CLR));  // open: Qn, preset, en
  or or_1 (or_1_out, L_i, S_t);
  D_Flip_Flop wait_2 (.clk(CLK), .D(demultiplexer_2_out1), .Q(S_t), .reset(CLR));  // open: Qn, preset, en
  D_Flip_Flop \while  (.clk(CLK), .D(or_1_out), .Q(while_q), .reset(CLR));  // open: Qn, preset, en
  Demultiplexer demultiplexer_2 (.out0(out_5), .out1(demultiplexer_2_out1), .in(while_q), .sel(in_4));  // open: en
  Demultiplexer demultiplexer_3 (
    .out0(out_10[0]), .out1(out_10[1]), .in(demultiplexer_2_out1), .sel(not_1_out));  // open: en
  not not_1 (not_1_out, in_3);
  or or_2 (or_2_out, out_5, GetC_q);
  D_Flip_Flop GetC (.clk(CLK), .D(or_2_out), .Q(GetC_q), .reset(CLR));  // open: Qn, preset, en
  or or_3 (L_n, L_n0, out_10[0], out_10[1]);
  or or_4 (L_t, L_n0, S_t);

  assign out_11 = L_i;

  // Other names for the same wires on the sheet: END = out_5; L_t0 = L_n0; L_t1 = S_t; n_2__0 = in_3;
  //   L_n1 = out_10[0]; S_n0 = out_10[0]; L_n2 = out_10[1]; S_n1 = out_10[1]; rst = CLR; SDir = L_i; t_i = in_4
endmodule
