// Logisim project Ordenación (Problema 67).circ as structural Verilog
module BOARD_BIG_ASM (
  output out_1
);

  wire button_1_out, CLK, CLR, d_ff_1_q, not_1_out, Write, Write_ASCII;
  wire [6:0] ASCII;
  wire [7:0] counter_1_q;
  wire [23:0] Dir_INPUT, Dir_MEMORY;
  wire [31:0] INPUT, MEMORY_IN, MEMORY_OUT;

  Button button_1 (.out(button_1_out));
  Clock clock_1 (.out(CLK));
  D_Flip_Flop d_ff_1 (.clk(CLK), .D(1'b1), .Q(d_ff_1_q), .reset(button_1_out));  // open: Qn, preset, en
  D_Flip_Flop d_ff_2 (.clk(CLK), .D(d_ff_1_q), .Qn(CLR), .reset(button_1_out));  // open: Q, preset, en
  BIG_ASM big_asm_1 (
    .DATA_INPUT(INPUT), .MEMORY_IN(MEMORY_OUT), .CLK(CLK), .CLR(CLR), .DIR_INPUT(Dir_INPUT),
    .MEMORY_OUT(MEMORY_IN), .DIR_MEMORY(Dir_MEMORY), .Write_OUTPUT(Write), .ASCII(ASCII),
    .Write_ASCII(Write_ASCII), .END(out_1));
  MEMORY memory_1 (.DIR(Dir_MEMORY), .DATA_IN(MEMORY_IN), .WRITE(Write), .CLK(CLK), .CLR(CLR), .DATA_OUT(MEMORY_OUT));
  INPUT input_1 (.DIR(Dir_INPUT), .CLK(CLK), .DATA_OUT(INPUT));
  Counter counter_1 (.load(1'b0), .count(not_1_out), .Q(counter_1_q), .clk(CLK), .clr(CLR));  // open: D, carry
  not not_1 (not_1_out, out_1);
  // Probe on counter_1_q
  TTY #(.rows(32), .cols(60)) tty_1 (.data(ASCII), .clk(CLK), .we(Write_ASCII), .clr(CLR));

  // Other names for the same wires on the sheet: END = out_1

  // Notes on the sheet:
  //   COUNTER
  //   BOARD
endmodule

module INPUT (
  input  [23:0] DIR,
  input  CLK,
  output [31:0] DATA_OUT
);

  RAM #(.addrWidth(24), .dataWidth(32)) ram_1 (.addr(DIR), .data(DATA_OUT), .clk(CLK), .ld(1'b1));  // open: sel, clr
endmodule

module MEMORY (
  input  [23:0] DIR,
  input  [31:0] DATA_IN,
  input  WRITE,
  input  CLK,
  input  CLR,
  output [31:0] DATA_OUT
);

  RAM #(.addrWidth(24), .dataWidth(32), .bus("separate")) ram_1 (
    .addr(DIR), .din(DATA_IN), .data(DATA_OUT), .str(WRITE), .clk(CLK), .clr(CLR));  // open: sel, ld
endmodule

module BIG_ASM (
  input  [31:0] DATA_INPUT,
  input  [31:0] MEMORY_IN,
  input  CLK,
  input  CLR,
  output [23:0] DIR_INPUT,
  output [31:0] MEMORY_OUT,
  output [23:0] DIR_MEMORY,
  output Write_OUTPUT,
  output [6:0] ASCII,
  output Write_ASCII,
  output END
);

  wire control_unit_1_load_c, control_unit_1_load_i, control_unit_1_load_m, control_unit_1_selector_m,
       I__C_M, I__M, I_C;
  wire [1:0] control_unit_1_selector_i;
  wire [31:24] Index;

  Control_Unit control_unit_1 (
    .Clock(CLK), .Start(CLR), .in_3({Index, DIR_INPUT}), .i__C(I_C), .I__M(I__M), .i__C_M(I__C_M), .END(END),
    .ASCII(ASCII), .Load_C(control_unit_1_load_c), .W_ASCII(Write_ASCII),
    .Selector_M(control_unit_1_selector_m), .Load_I(control_unit_1_load_i),
    .Selector_I(control_unit_1_selector_i), .Load_M(control_unit_1_load_m));
  Data_Path data_path_1 (
    .in_1(CLK), .Ram_Out(DATA_INPUT), .Load_C(control_unit_1_load_c), .Load_i(control_unit_1_load_i),
    .Load_m(control_unit_1_load_m), .Selector_I(control_unit_1_selector_i),
    .Selector_M(control_unit_1_selector_m), .I__C(I_C), .I({Index, DIR_INPUT}), .I__C_M(I__C_M), .i__M(I__M));

  assign Write_OUTPUT = Write_ASCII;

  // Other names for the same wires on the sheet: Index[23:0] = DIR_INPUT; Ram_Out[31:0] = DATA_INPUT;
  //   W_ASCII = Write_ASCII
endmodule

module PRINT_UDEC (
  input  [31:0] num,
  input  start,
  input  CLK,
  input  RST,
  output [6:0] ASCII,
  output Write_ASCII,
  output \end 
);

  wire _0_c, _0_n, demultiplexer_1_out0, demultiplexer_2_out0, demultiplexer_2_out1, demultiplexer_3_out0,
       demultiplexer_3_out1, IDLE_2_q, IDLE_3_q, IDLE_4_q, IDLE_q, Lc, Lc_0, Ln, Ln_0, or_1_out;
  wire [23:0] bit_extender_1_out;
  wire [31:0] c, c___1, c___1_t, divider_1_rem, memory_1_data_out, multiplexer_1_out, multiplexer_2_out,
       multiplexer_3_out, n, n___10, n___10___48;

  Multiplexer #(.width(32), .enable("false")) multiplexer_1 (
    .in0(num), .in1(n___10), .out(multiplexer_1_out), .sel(Lc_0));
  Divider #(.width(32)) divider_1 (.a(n), .b(32'ha), .out(n___10), .rem(divider_1_rem));  // open: upper
  Adder #(.width(32)) adder_1 (.a(divider_1_rem), .b(32'h30), .out(n___10___48));  // open: cin, cout
  or or_1 (or_1_out, demultiplexer_1_out0, \end );
  Register #(.width(32)) u_n (.D(multiplexer_1_out), .en(Ln), .Q(n), .clk(CLK), .clr(RST));
  D_Flip_Flop IDLE (.clk(CLK), .D(or_1_out), .Q(IDLE_q), .preset(RST));  // open: Qn, en, reset
  Demultiplexer #(.enable("false")) demultiplexer_1 (
    .out0(demultiplexer_1_out0), .out1(Ln_0), .in(IDLE_q), .sel(start));
  or or_2 (Write_ASCII, demultiplexer_3_out0, demultiplexer_2_out1);
  Multiplexer #(.width(32), .enable("false")) multiplexer_2 (
    .in0(c___1), .in1(c___1_t), .out(multiplexer_2_out), .sel(Write_ASCII));
  Adder #(.width(32)) adder_2 (.a(c), .b(32'h1), .out(c___1));  // open: cin, cout
  Subtractor #(.width(32)) subtractor_1 (.a(c), .b(32'h1), .out(c___1_t));  // open: bin, bout
  D_Flip_Flop IDLE_2 (.clk(CLK), .D(Ln_0), .Q(IDLE_2_q), .reset(RST));  // open: Qn, preset, en
  Register #(.width(32)) u_c (.D(multiplexer_2_out), .en(Lc), .Q(c), .clk(CLK), .clr(RST));
  or or_3 (Lc_0, IDLE_2_q, demultiplexer_3_out1);
  Multiplexer #(.width(32), .enable("false")) multiplexer_3 (
    .in0(c), .in1(c___1_t), .out(multiplexer_3_out), .sel(Write_ASCII));
  Comparator #(.width(32), .mode("unsigned")) comparator_1 (.a({32{1'b0}}), .b(n), .lt(_0_n));  // open: gt, eq
  Comparator #(.width(32), .mode("unsigned")) comparator_2 (.a({32{1'b0}}), .b(c), .lt(_0_c));  // open: gt, eq
  D_Flip_Flop IDLE_3 (.clk(CLK), .D(Write_ASCII), .Q(IDLE_3_q), .reset(RST));  // open: Qn, preset, en
  Demultiplexer #(.enable("false")) demultiplexer_2 (
    .out0(demultiplexer_2_out0), .out1(demultiplexer_2_out1), .in(IDLE_3_q), .sel(_0_c));
  Bit_Extender #(.in_width(32), .out_width(24)) bit_extender_1 (.in(multiplexer_3_out), .out(bit_extender_1_out));
  D_Flip_Flop IDLE_4 (.clk(CLK), .D(Lc_0), .Q(IDLE_4_q), .reset(RST));  // open: Qn, preset, en
  or or_4 (Lc, Lc_0, Write_ASCII);
  or or_5 (Ln, Ln_0, Lc_0);
  Demultiplexer #(.enable("false")) demultiplexer_3 (
    .out0(demultiplexer_3_out0), .out1(demultiplexer_3_out1), .in(IDLE_4_q), .sel(_0_n));
  D_Flip_Flop IDLE_5 (.clk(CLK), .D(demultiplexer_2_out0), .Q(\end ), .reset(RST));  // open: Qn, preset, en
  MEMORY memory_1 (
    .DIR(bit_extender_1_out), .DATA_IN(n___10___48), .WRITE(Lc_0), .CLK(CLK), .CLR(RST),
    .DATA_OUT(memory_1_data_out));
  Bit_Extender #(.in_width(32), .out_width(7)) bit_extender_2 (.in(memory_1_data_out), .out(ASCII));

  // Other names for the same wires on the sheet: Lc_1 = Write_ASCII; Sc = Write_ASCII; Ln_1 = Lc_0; Sn = Lc_0;
  //   Write = Lc_0
endmodule

module PRINT_DEC (
  input  [31:0] num,
  input  start,
  input  CLK,
  input  RST,
  output [6:0] ASCII,
  output Write_ASCII,
  output END
);

  wire demultiplexer_1_out0, demultiplexer_1_out1, demultiplexer_2_out0, demultiplexer_3_out0, end_t,
       IDLE_3_q, IDLE_q, or_1_out, or_2_out, or_3_out, S_ASCII, startUDEC, Write_ASCII_1;
  wire [6:0] ASCII_t;
  wire [31:0] multiplexer_1_out, negator_1_out;

  or or_1 (or_1_out, demultiplexer_1_out0, END);
  Negator #(.width(32)) negator_1 (.in(num), .out(negator_1_out));
  D_Flip_Flop IDLE (.clk(CLK), .D(or_1_out), .Q(IDLE_q), .preset(RST));  // open: Qn, en, reset
  Demultiplexer #(.enable("false")) demultiplexer_1 (
    .out0(demultiplexer_1_out0), .out1(demultiplexer_1_out1), .in(IDLE_q), .sel(start));
  Multiplexer #(.width(32), .enable("false")) multiplexer_1 (
    .in0(num), .in1(negator_1_out), .out(multiplexer_1_out), .sel(num[31]));
  Demultiplexer #(.enable("false")) demultiplexer_2 (
    .out0(demultiplexer_2_out0), .out1(S_ASCII), .in(demultiplexer_1_out1), .sel(num[31]));
  or or_2 (or_2_out, demultiplexer_2_out0, S_ASCII);
  D_Flip_Flop IDLE_2 (.clk(CLK), .D(or_2_out), .Q(startUDEC), .reset(RST));  // open: Qn, preset, en
  PRINT_UDEC print_udec_1 (
    .num(multiplexer_1_out), .start(startUDEC), .CLK(CLK), .RST(RST), .ASCII(ASCII_t),
    .Write_ASCII(Write_ASCII_1), .\end (end_t));
  D_Flip_Flop IDLE_3 (.clk(CLK), .D(or_3_out), .Q(IDLE_3_q), .reset(RST));  // open: Qn, preset, en
  or or_3 (or_3_out, startUDEC, demultiplexer_3_out0);
  Demultiplexer #(.enable("false")) demultiplexer_3 (
    .out0(demultiplexer_3_out0), .out1(END), .in(IDLE_3_q), .sel(end_t));
  Multiplexer #(.width(7), .enable("false")) multiplexer_2 (
    .in0(ASCII_t), .in1(7'b0101101), .out(ASCII), .sel(S_ASCII));
  or or_4 (Write_ASCII, S_ASCII, Write_ASCII_1);

  // Other names for the same wires on the sheet: sign = num[31]; Write_ASCII_0 = S_ASCII
endmodule

module TEST_PRINT (
  input  [31:0] in_1,
  output out_2
);

  wire button_1_out, button_2_out, CLK, CLR, d_ff_1_q, Write_ASCII;
  wire [6:0] ASCII;

  Button button_1 (.out(button_1_out));
  Clock clock_1 (.out(CLK));
  D_Flip_Flop d_ff_1 (.clk(CLK), .D(1'b1), .Q(d_ff_1_q), .reset(button_1_out));  // open: Qn, preset, en
  D_Flip_Flop d_ff_2 (.clk(CLK), .D(d_ff_1_q), .Qn(CLR), .reset(button_1_out));  // open: Q, preset, en
  Button button_2 (.out(button_2_out));
  PRINT_UDEC print_udec_1 ();  // open: num, start, CLK, RST, ASCII, Write_ASCII, end
  PRINT_DEC print_dec_1 (
    .num(in_1), .start(button_2_out), .CLK(CLK), .RST(CLR), .ASCII(ASCII), .Write_ASCII(Write_ASCII),
    .END(out_2));
  TTY #(.rows(32), .cols(60)) tty_1 (.data(ASCII), .clk(CLK), .we(Write_ASCII), .clr(CLR));
endmodule

module Control_Unit (
  input  Clock,
  input  Start,
  input  [31:0] in_3,
  input  i__C,
  input  I__M,
  input  i__C_M,
  output END,
  output [6:0] ASCII,
  output Load_C,
  output W_ASCII,
  output Selector_M,
  output Load_I,
  output [1:0] Selector_I,
  output Load_M
);

  wire and_1_out, CLR, d_ff_1_q, d_ff_2_q, d_ff_4_q, demultiplexer_1_out0, demultiplexer_2_out1,
       demultiplexer_3_out0, demultiplexer_4_out0, demultiplexer_4_out1, demultiplexer_5_out1, END_q, IDLE_q,
       Lc0, Li1, Li2, Li3, not_1_out, or_1_out, or_5_out, or_8_out, or_9_out, or_10_out, or_11_out,
       or_12_out, print_dec_1_end, print_dec_1_write_ascii, While_2_q, While_q;
  wire [6:0] print_dec_1_ascii;

  or or_1 (or_1_out, demultiplexer_1_out0, demultiplexer_5_out1);
  not not_1 (not_1_out, Start);
  Demultiplexer #(.enable("false")) demultiplexer_1 (
    .out0(demultiplexer_1_out0), .out1(Lc0), .in(IDLE_q), .sel(d_ff_1_q));
  D_Flip_Flop IDLE (.clk(Clock), .D(or_1_out), .Q(IDLE_q), .preset(d_ff_1_q));  // open: Qn, en, reset
  D_Flip_Flop d_ff_1 (.clk(Clock), .D(Start), .Q(d_ff_1_q), .reset(not_1_out));  // open: Qn, preset, en
  or or_2 (Load_M, Lc0, Selector_M);
  or or_3 (Load_I, Lc0, Li1, Li2, Li3);
  buf or_4 (Load_C, Lc0);  // OR_Gate
  or or_5 (or_5_out, Lc0, Li1);
  or or_6 (Selector_I[0], Li1, Li3);
  buf or_7 (Selector_I[1], Li2);  // OR_Gate
  D_Flip_Flop While (.clk(Clock), .D(or_5_out), .Q(While_q));  // open: Qn, preset, en, reset
  Demultiplexer #(.enable("false")) demultiplexer_2 (.out0(Li2), .out1(demultiplexer_2_out1), .in(While_q), .sel(i__C));
  Demultiplexer #(.enable("false")) demultiplexer_3 (
    .out0(demultiplexer_3_out0), .out1(Selector_M), .in(demultiplexer_2_out1), .sel(I__M));
  D_Flip_Flop d_ff_2 (.clk(Clock), .D(1'b1), .Q(d_ff_2_q));  // open: Qn, preset, en, reset
  or or_8 (or_8_out, demultiplexer_3_out0, Selector_M);
  D_Flip_Flop After_IF (.clk(Clock), .D(or_8_out), .Q(Li1));  // open: Qn, preset, en, reset
  D_Flip_Flop d_ff_3 (.clk(Clock), .D(d_ff_2_q), .Qn(CLR));  // open: Q, preset, en, reset
  or or_9 (or_9_out, demultiplexer_4_out1, Li3);
  or or_10 (or_10_out, Li2, or_9_out);
  D_Flip_Flop While_2 (.clk(Clock), .D(or_10_out), .Q(While_2_q));  // open: Qn, preset, en, reset
  Demultiplexer #(.enable("false")) demultiplexer_4 (
    .out0(demultiplexer_4_out0), .out1(demultiplexer_4_out1), .in(While_2_q), .sel(i__C_M));
  D_Flip_Flop After_Print (.clk(Clock), .D(d_ff_4_q), .Q(Li3));  // open: Qn, preset, en, reset
  or or_11 (or_11_out, END, demultiplexer_4_out0);
  and and_1 (and_1_out, demultiplexer_4_out1, ~W_ASCII);  // AND_Gate
  D_Flip_Flop u_END (.clk(Clock), .D(or_11_out), .Q(END_q));  // open: Qn, preset, en, reset
  Demultiplexer #(.enable("false")) demultiplexer_5 (.out0(END), .out1(demultiplexer_5_out1), .in(END_q), .sel(Start));
  PRINT_DEC print_dec_1 (
    .num(in_3), .start(and_1_out), .CLK(Clock), .RST(CLR), .ASCII(print_dec_1_ascii),
    .Write_ASCII(print_dec_1_write_ascii), .END(print_dec_1_end));
  Multiplexer #(.width(7), .enable("false")) multiplexer_1 (
    .in0(print_dec_1_ascii), .in1(7'b0100000), .out(ASCII), .sel(d_ff_4_q));
  D_Flip_Flop d_ff_4 (.clk(Clock), .D(print_dec_1_end), .Q(d_ff_4_q));  // open: Qn, preset, en, reset
  or or_12 (or_12_out, d_ff_4_q, print_dec_1_write_ascii);
  and and_2 (W_ASCII, or_12_out, ~END);  // AND_Gate

  // Other names for the same wires on the sheet: CLK = Clock; I[31:0] = in_3; Lc = Load_C; Li = Load_I; Lm = Load_M;
  //   Li0 = Lc0; Lm0 = Lc0; Si_0 = Selector_I[0]; Si_1 = Selector_I[1]; Si_0_0 = Li1; Si_0_2 = Li3; Si_1_0 = Li2;
  //   Lm1 = Selector_M; Sm = Selector_M
endmodule

module Data_Path (
  input  in_1,
  input  [31:0] Ram_Out,
  input  Load_C,
  input  Load_i,
  input  Load_m,
  input  [1:0] Selector_I,
  input  Selector_M,
  output I__C,
  output [31:0] I,
  output I__C_M,
  output i__M
);

  wire comparator_1_eq, comparator_1_lt, comparator_2_eq, comparator_2_lt;
  wire [31:0] adder_1_out, C, i_1, M, multiplexer_1_out, multiplexer_2_out, subtractor_1_out;

  Adder #(.width(32)) adder_1 (.a(C), .b(M), .out(adder_1_out));  // open: cin, cout
  Subtractor #(.width(32)) subtractor_1 (.a(adder_1_out), .b(32'h1), .out(subtractor_1_out));  // open: bin, bout
  Comparator #(.width(32)) comparator_1 (.a(I), .b(C), .eq(comparator_1_eq), .lt(comparator_1_lt));  // open: gt
  or or_1 (I__C, comparator_1_eq, comparator_1_lt);
  Comparator #(.width(32)) comparator_2 (
    .a(I), .b(subtractor_1_out), .eq(comparator_2_eq), .lt(comparator_2_lt));  // open: gt
  Comparator #(.width(32), .mode("unsigned")) comparator_3 (.a(Ram_Out), .b(M), .lt(i__M));  // open: gt, eq
  Multiplexer #(.select(2), .width(32)) multiplexer_1 (
    .in0(32'h1), .in1(i_1), .in2(M), .out(multiplexer_1_out), .sel(Selector_I));  // open: in3, en
  or or_2 (I__C_M, comparator_2_eq, comparator_2_lt);
  Register #(.width(32)) u_C (.D(Ram_Out), .en(Load_C), .Q(C), .clk(in_1));  // open: clr
  Register #(.width(32)) u_I (.D(multiplexer_1_out), .en(Load_i), .Q(I), .clk(in_1));  // open: clr
  Adder #(.width(32)) adder_2 (.a(I), .b(32'h1), .out(i_1));  // open: cin, cout
  Multiplexer #(.width(32)) multiplexer_2 (
    .in0(32'h7fffffff), .in1(Ram_Out), .out(multiplexer_2_out), .sel(Selector_M));  // open: en
  Register #(.width(32)) u_M (.D(multiplexer_2_out), .en(Load_m), .Q(M), .clk(in_1));  // open: clr

  // Other names for the same wires on the sheet: Clock = in_1; Lc = Load_C; Li = Load_i; Lm = Load_m;
  //   Si[1:0] = Selector_I; Sm = Selector_M
endmodule
